// Logisim project PBPUMk4.circ as structural Verilog: 1 circuit, main circuit main
module main (
);

  wire CLK_out, instructiondecoder_1_inst, instructiondecoder_1_num;
  wire [3:0] INST_out;
  wire [7:0] counter_1_q, rom_1_data;

  Counter counter_1 (.Q(counter_1_q), .clk(instructiondecoder_1_inst));  // open: load, D, count, carry, up, clr
  Clock CLK (.out(CLK_out));
  ROM rom_1 (.addr(counter_1_q), .data(rom_1_data));
  RAM ram_1 ();  // open: addr, we, oe, clk, din, dout
  assign INST_out = instructiondecoder_1_inst ? rom_1_data[3:0] : 4'bz;  // Controlled_Buffer INST
  assign INST_out = instructiondecoder_1_num ? rom_1_data[7:4] : 4'bz;  // Controlled_Buffer NUM
  // Probe on rom_1_data
  InstructionDecoder instructiondecoder_1 (
    .INST(instructiondecoder_1_inst), .NUM(instructiondecoder_1_num), .D0(INST_out[0]), .D1(INST_out[1]),
    .D2(INST_out[2]), .D3(INST_out[3]), .CLK(CLK_out));  // open: JMP_Out, RTX_Out, RTY_Out, USC_Out, NOP_Out, ADD_Out, SUB_Out, WT1_Out, WT2_Out, WTX_Out, WTY_Out, WTZ_Out, ZTR_Out, RTZ_Out, PC1_Out, PC2_Out

  // Notes on the sheet:
  //   contents of rom_1 (hex, n*v repeats v):
  //   0 30 40 79 80 42 79 80 43 76 80
endmodule
